// Logisim project MIPS32.circ as structural Verilog
module main (
);

  wire alu_1_zf, and_1_out, control_1_alusrc, control_1_branch, control_1_memtoreg, MemRead, MemWrite,
       RegDst, Write;
  wire [4:0] multiplexer_2_out;
  wire [5:0] ALUop;
  wire [10:0] alucontrol_1_alufunc;
  wire [31:0] adder_1_out, adder_2_out, alu_1_result, data_1_readdata, instructions_1_instruction,
       multiplexer_1_out, multiplexer_3_out, multiplexer_4_out, multiplexer_5_out, PC_q,
       RegisterFile_readdata1, RegisterFile_readdata2, shifter_1_out, signextend_1_value_u32;

  Register #(.width(32)) PC (.D(multiplexer_1_out), .en(1'b1), .Q(PC_q));  // open: clk, clr
  Multiplexer #(.width(32)) multiplexer_1 (
    .in0(multiplexer_4_out), .in1(multiplexer_5_out), .out(multiplexer_1_out));  // open: sel
  // CLKmodul clkmodul_1: pin names not known
  Instructions instructions_1 (.Read(PC_q), .Instruction(instructions_1_instruction));
  Adder #(.width(32)) adder_1 (.a(PC_q), .b(32'h4), .out(adder_1_out));  // open: cin, cout
  Multiplexer #(.width(5)) multiplexer_2 (
    .in0(instructions_1_instruction[20:16]), .in1(instructions_1_instruction[15:11]),
    .out(multiplexer_2_out), .sel(RegDst));
  Control control_1 (
    .Opcode(instructions_1_instruction[31:26]), .RegDst(RegDst), .Branch(control_1_branch),
    .MemRead(MemRead), .MemToReg(control_1_memtoreg), .MemWrite(MemWrite), .ALUSrc(control_1_alusrc),
    .RegWrite(Write), .ALUop(ALUop));
  Registers RegisterFile (
    .ReadRegister1(instructions_1_instruction[25:21]), .ReadRegister2(instructions_1_instruction[20:16]),
    .WriteRegister(multiplexer_2_out), .WriteData(multiplexer_5_out), .Write(Write),
    .ReadData1(RegisterFile_readdata1), .ReadData2(RegisterFile_readdata2));  // open: PCtoReg31, PC
  SignExtend signextend_1 (.Value_u16(instructions_1_instruction[15:0]), .Value_u32(signextend_1_value_u32));
  Multiplexer #(.width(32)) multiplexer_3 (
    .in0(RegisterFile_readdata2), .in1(signextend_1_value_u32), .out(multiplexer_3_out));  // open: sel
  ALUControl alucontrol_1 (
    .SHAMT(instructions_1_instruction[10:6]), .ALUop(ALUop), .Func(instructions_1_instruction[5:0]),
    .ALUFunc(alucontrol_1_alufunc));
  Shifter #(.width(32)) shifter_1 (.in(signextend_1_value_u32), .\dist (5'b00010), .out(shifter_1_out));
  Adder #(.width(32)) adder_2 (.a(adder_1_out), .b(shifter_1_out), .out(adder_2_out));  // open: cin, cout
  and and_1 (and_1_out, control_1_branch, alu_1_zf);
  ALU alu_1 (
    .Operand1(RegisterFile_readdata1), .Operand2(multiplexer_3_out), .ALUfunc(alucontrol_1_alufunc),
    .ZF(alu_1_zf), .Result(alu_1_result));
  Multiplexer #(.width(32)) multiplexer_4 (
    .in0(adder_1_out), .in1(adder_2_out), .out(multiplexer_4_out), .sel(and_1_out));
  Data data_1 (
    .Address(alu_1_result), .MemWrite(MemWrite), .MemRead(MemRead), .WriteData(RegisterFile_readdata2),
    .ReadData(data_1_readdata));
  Multiplexer #(.width(32)) multiplexer_5 (
    .in0(alu_1_result), .in1(data_1_readdata), .out(multiplexer_5_out), .sel(control_1_memtoreg));
endmodule

module Registers (
  input  [4:0] ReadRegister1,
  input  [4:0] ReadRegister2,
  input  [4:0] WriteRegister,
  input  [31:0] WriteData,
  input  Write,
  input  PCtoReg31,
  input  [31:0] PC,
  output [31:0] ReadData1,
  output [31:0] ReadData2
);

  wire decoder_1_out0, decoder_1_out1, decoder_1_out2, decoder_1_out3, decoder_1_out4, decoder_1_out5,
       decoder_1_out6, decoder_1_out7, decoder_1_out8, decoder_1_out9, decoder_1_out10, decoder_1_out11,
       decoder_1_out12, decoder_1_out13, decoder_1_out14, decoder_1_out15, decoder_1_out16, decoder_1_out17,
       decoder_1_out18, decoder_1_out19, decoder_1_out20, decoder_1_out21, decoder_1_out22, decoder_1_out23,
       decoder_1_out24, decoder_1_out25, decoder_1_out26, decoder_1_out27, decoder_1_out28, decoder_1_out29,
       decoder_1_out30, decoder_1_out31;
  wire [31:0] multiplexer_1_out, register_1_q, register_2_q, register_3_q, register_4_q, register_5_q,
       register_6_q, register_7_q, register_8_q, register_9_q, register_10_q, register_11_q, register_12_q,
       register_13_q, register_14_q, register_15_q, register_16_q, register_17_q, register_18_q,
       register_19_q, register_20_q, register_21_q, register_22_q, register_23_q, register_24_q,
       register_25_q, register_26_q, register_27_q, register_28_q, register_29_q, register_30_q,
       register_31_q, register_32_q;

  Decoder #(.select(5)) decoder_1 (
    .out0(decoder_1_out0), .out1(decoder_1_out1), .out2(decoder_1_out2), .out3(decoder_1_out3),
    .out4(decoder_1_out4), .out5(decoder_1_out5), .out6(decoder_1_out6), .out7(decoder_1_out7),
    .out8(decoder_1_out8), .out9(decoder_1_out9), .out10(decoder_1_out10), .out11(decoder_1_out11),
    .out12(decoder_1_out12), .out13(decoder_1_out13), .out14(decoder_1_out14), .out15(decoder_1_out15),
    .out16(decoder_1_out16), .out17(decoder_1_out17), .out18(decoder_1_out18), .out19(decoder_1_out19),
    .out20(decoder_1_out20), .out21(decoder_1_out21), .out22(decoder_1_out22), .out23(decoder_1_out23),
    .out24(decoder_1_out24), .out25(decoder_1_out25), .out26(decoder_1_out26), .out27(decoder_1_out27),
    .out28(decoder_1_out28), .out29(decoder_1_out29), .out30(decoder_1_out30), .out31(decoder_1_out31),
    .sel(WriteRegister), .en(Write));
  Multiplexer #(.width(32)) multiplexer_1 (.in0(WriteData), .in1(PC), .out(multiplexer_1_out), .sel(PCtoReg31));
  Register #(.width(32)) register_1 (.D(WriteData), .en(decoder_1_out0), .Q(register_1_q));  // open: clk, clr
  Register #(.width(32)) register_2 (.D(WriteData), .en(decoder_1_out1), .Q(register_2_q));  // open: clk, clr
  Register #(.width(32)) register_3 (.D(WriteData), .en(decoder_1_out2), .Q(register_3_q));  // open: clk, clr
  Register #(.width(32)) register_4 (.D(WriteData), .en(decoder_1_out3), .Q(register_4_q));  // open: clk, clr
  Register #(.width(32)) register_5 (.D(WriteData), .en(decoder_1_out4), .Q(register_5_q));  // open: clk, clr
  Register #(.width(32)) register_6 (.D(WriteData), .en(decoder_1_out5), .Q(register_6_q));  // open: clk, clr
  Register #(.width(32)) register_7 (.D(WriteData), .en(decoder_1_out6), .Q(register_7_q));  // open: clk, clr
  Register #(.width(32)) register_8 (.D(WriteData), .en(decoder_1_out7), .Q(register_8_q));  // open: clk, clr
  Register #(.width(32)) register_9 (.D(WriteData), .en(decoder_1_out8), .Q(register_9_q));  // open: clk, clr
  Register #(.width(32)) register_10 (.D(WriteData), .en(decoder_1_out9), .Q(register_10_q));  // open: clk, clr
  Register #(.width(32)) register_11 (.D(WriteData), .en(decoder_1_out10), .Q(register_11_q));  // open: clk, clr
  Register #(.width(32)) register_12 (.D(WriteData), .en(decoder_1_out11), .Q(register_12_q));  // open: clk, clr
  Register #(.width(32)) register_13 (.D(WriteData), .en(decoder_1_out12), .Q(register_13_q));  // open: clk, clr
  Register #(.width(32)) register_14 (.D(WriteData), .en(decoder_1_out13), .Q(register_14_q));  // open: clk, clr
  Register #(.width(32)) register_15 (.D(WriteData), .en(decoder_1_out14), .Q(register_15_q));  // open: clk, clr
  Register #(.width(32)) register_16 (.D(WriteData), .en(decoder_1_out15), .Q(register_16_q));  // open: clk, clr
  Register #(.width(32)) register_17 (.D(WriteData), .en(decoder_1_out16), .Q(register_17_q));  // open: clk, clr
  Register #(.width(32)) register_18 (.D(WriteData), .en(decoder_1_out17), .Q(register_18_q));  // open: clk, clr
  Register #(.width(32)) register_19 (.D(WriteData), .en(decoder_1_out18), .Q(register_19_q));  // open: clk, clr
  Register #(.width(32)) register_20 (.D(WriteData), .en(decoder_1_out19), .Q(register_20_q));  // open: clk, clr
  Register #(.width(32)) register_21 (.D(WriteData), .en(decoder_1_out20), .Q(register_21_q));  // open: clk, clr
  Register #(.width(32)) register_22 (.D(WriteData), .en(decoder_1_out21), .Q(register_22_q));  // open: clk, clr
  Register #(.width(32)) register_23 (.D(WriteData), .en(decoder_1_out22), .Q(register_23_q));  // open: clk, clr
  Register #(.width(32)) register_24 (.D(WriteData), .en(decoder_1_out23), .Q(register_24_q));  // open: clk, clr
  Register #(.width(32)) register_25 (.D(WriteData), .en(decoder_1_out24), .Q(register_25_q));  // open: clk, clr
  Register #(.width(32)) register_26 (.D(WriteData), .en(decoder_1_out25), .Q(register_26_q));  // open: clk, clr
  Register #(.width(32)) register_27 (.D(WriteData), .en(decoder_1_out26), .Q(register_27_q));  // open: clk, clr
  Register #(.width(32)) register_28 (.D(WriteData), .en(decoder_1_out27), .Q(register_28_q));  // open: clk, clr
  Register #(.width(32)) register_29 (.D(WriteData), .en(decoder_1_out28), .Q(register_29_q));  // open: clk, clr
  Register #(.width(32)) register_30 (.D(WriteData), .en(decoder_1_out29), .Q(register_30_q));  // open: clk, clr
  Register #(.width(32)) register_31 (.D(WriteData), .en(decoder_1_out30), .Q(register_31_q));  // open: clk, clr
  Register #(.width(32)) register_32 (
    .D(multiplexer_1_out), .en(decoder_1_out31), .Q(register_32_q));  // open: clk, clr
  Multiplexer #(.select(5), .width(32)) multiplexer_2 (
    .in0(register_1_q), .in1(register_2_q), .in2(register_3_q), .in3(register_4_q), .in4(register_5_q),
    .in5(register_6_q), .in6(register_7_q), .in7(register_8_q), .in8(register_9_q), .in9(register_10_q),
    .in10(register_11_q), .in11(register_12_q), .in12(register_13_q), .in13(register_14_q),
    .in14(register_15_q), .in15(register_16_q), .in16(register_17_q), .in17(register_18_q),
    .in18(register_19_q), .in19(register_20_q), .in20(register_21_q), .in21(register_22_q),
    .in22(register_23_q), .in23(register_24_q), .in24(register_25_q), .in25(register_26_q),
    .in26(register_27_q), .in27(register_28_q), .in28(register_29_q), .in29(register_30_q),
    .in30(register_31_q), .in31(register_32_q), .out(ReadData1), .sel(ReadRegister1));
  Multiplexer #(.select(5), .width(32)) multiplexer_3 (
    .in0(register_1_q), .in1(register_2_q), .in2(register_3_q), .in3(register_4_q), .in4(register_5_q),
    .in5(register_6_q), .in6(register_7_q), .in7(register_8_q), .in8(register_9_q), .in9(register_10_q),
    .in10(register_11_q), .in11(register_12_q), .in12(register_13_q), .in13(register_14_q),
    .in14(register_15_q), .in15(register_16_q), .in16(register_17_q), .in17(register_18_q),
    .in18(register_19_q), .in19(register_20_q), .in20(register_21_q), .in21(register_22_q),
    .in22(register_23_q), .in23(register_24_q), .in24(register_25_q), .in25(register_26_q),
    .in26(register_27_q), .in27(register_28_q), .in28(register_29_q), .in29(register_30_q),
    .in30(register_31_q), .in31(register_32_q), .out(ReadData2), .sel(ReadRegister2));

  // Other names for the same wires on the sheet: WD[31:0] = WriteData
endmodule

module ALU (
  input  [31:0] Operand1,
  input  [31:0] Operand2,
  input  [10:0] ALUfunc,
  output ZF,
  output [31:0] Result
);

  wire [31:0] Add, aright, BAnd, bnor, bor, bxor, logleft, logright, lui, multiplexer_1_out,
       multiplexer_2_out, shifter_1_out, slt, sub;

  Shifter #(.width(32)) shifter_1 (.in(Operand2), .\dist (5'b01111), .out(shifter_1_out));
  Shifter shifter_2 ();  // open: in, dist, out
  Shifter #(.width(32)) shifter_3 (.in(Operand1), .\dist (ALUfunc[4:0]), .out(logleft));
  Shifter #(.shift("lr"), .width(32)) shifter_4 (.in(Operand1), .\dist (ALUfunc[4:0]), .out(logright));
  Shifter #(.shift("ar"), .width(32)) shifter_5 (.in(Operand1), .\dist (ALUfunc[4:0]), .out(aright));
  Shifter #(.shift("rl"), .width(32)) shifter_6 (.in(Operand1), .\dist (ALUfunc[4:0]));  // open: out
  Shifter #(.shift("rr"), .width(32)) shifter_7 (.in(Operand1), .\dist (ALUfunc[4:0]));  // open: out
  Adder #(.width(32)) adder_1 (.a(Operand1), .b(Operand2), .out(Add));  // open: cin, cout
  Subtractor #(.width(32)) subtractor_1 (.a(Operand1), .b(Operand2), .out(sub));  // open: bin, bout
  assign BAnd = Operand1 & Operand2;  // AND_Gate and_1, 32 bits wide
  assign bor = Operand1 | Operand2;  // OR_Gate or_1, 32 bits wide
  // NOT_Gate not_1 has open pins: in=Operand1, out=open
  assign bxor = Operand1 ^ Operand2;  // XOR_Gate xor_1, 32 bits wide
  Negator #(.width(32)) negator_1 (.in(Operand1));  // open: out
  sltkolo sltkolo_1 (.operand1(Operand1), .operand2(Operand2), .out_3(slt));
  Adder #(.width(32)) adder_2 (.a(Operand1), .b(shifter_1_out), .out(lui));  // open: cin, cout
  Adder adder_3 ();  // open: a, b, out, cin, cout
  assign bnor = ~bor;  // NOT_Gate not_2, 32 bits wide
  Multiplexer #(.select(5), .width(32)) multiplexer_1 (
    .in0(logleft), .in2(logright), .in3(aright), .in8(Operand1), .in17(lui), .out(multiplexer_1_out),
    .sel(ALUfunc[9:5]));  // open: in1, in4, in5, in6, in7, in9, in10, in11, in12, in13, in14, in15, in16, in18, in19, in20, in21, in22, in23, in24, in25, in26, in27, in28, in29, in30, in31
  Multiplexer #(.select(5), .width(32)) multiplexer_2 (
    .in0(Add), .in2(sub), .in4(BAnd), .in5(bor), .in6(bxor), .in7(bnor), .in10(slt), .out(multiplexer_2_out));  // open: in1, in3, in8, in9, in11, in12, in13, in14, in15, in16, in17, in18, in19, in20, in21, in22, in23, in24, in25, in26, in27, in28, in29, in30, in31, sel
  Multiplexer #(.width(32)) multiplexer_3 (
    .in0(multiplexer_1_out), .in1(multiplexer_2_out), .out(Result), .sel(ALUfunc[10]));
  and and_2 (ZF, ~Result[0], ~Result[1], ~Result[2], ~Result[3], ~Result[4], ~Result[5], ~Result[6], ~Result[7], ~Result[8], ~Result[9], ~Result[10], ~Result[11], ~Result[12], ~Result[13], ~Result[14], ~Result[15], ~Result[17], ~Result[18], ~Result[19], ~Result[20], ~Result[21], ~Result[22], ~Result[23], ~Result[24], ~Result[25], ~Result[26], ~Result[27], ~Result[28], ~Result[29], ~Result[30], ~Result[31], ~Result[16]);  // AND_Gate

  // Other names for the same wires on the sheet: allpass[31:0] = Operand1; LS[4:0] = ALUfunc[9:5]; HS = ALUfunc[10]

  // Notes on the sheet:
  //   velicina?
endmodule

module Data (
  input  [31:0] Address,
  input  MemWrite,
  input  MemRead,
  input  [31:0] WriteData,
  output [31:0] ReadData
);

  RAM ram_1 (
    .addr(Address[7:0]), .we(MemWrite), .oe(MemRead), .din(WriteData[7:0]), .dout(ReadData[7:0]));  // open: clk
  RAM ram_2 (
    .addr(Address[15:8]), .we(MemWrite), .oe(MemRead), .din(WriteData[15:8]), .dout(ReadData[15:8]));  // open: clk
  RAM ram_3 (
    .addr(Address[23:16]), .we(MemWrite), .oe(MemRead), .din(WriteData[23:16]), .dout(ReadData[23:16]));  // open: clk
  RAM ram_4 (
    .addr(Address[31:24]), .we(MemWrite), .oe(MemRead), .din(WriteData[31:24]), .dout(ReadData[31:24]));  // open: clk
endmodule

module Instructions (
  input  [31:0] Read,
  output [31:0] Instruction
);

  ROM #(.addrWidth(16), .dataWidth(32)) rom_1 (.addr(Read[15:0]), .data(Instruction));
endmodule

module SignExtend (
  input  [15:0] Value_u16,
  output [31:0] Value_u32
);


  assign Value_u32 = {{17{Value_u16[15]}}, Value_u16[14:0]};
endmodule

module Control (
  input  [5:0] Opcode,
  output RegDst,
  output Branch,
  output MemRead,
  output MemToReg,
  output MemWrite,
  output ALUSrc,
  output RegWrite,
  output [5:0] ALUop
);

  wire [4:4] rom_1_data;

  ROM #(.addrWidth(6)) rom_1 (
    .addr(Opcode), .data({RegWrite, ALUSrc, MemWrite, rom_1_data[4], MemToReg, MemRead, Branch, RegDst}));
  ROM #(.addrWidth(6), .dataWidth(6)) rom_2 (.addr(Opcode), .data(ALUop));

  // Notes on the sheet:
  //   contents of rom_1 (hex, n*v repeats v):
  //   0 0 4*42 0 0 3 0 3 0 3 3 0 1 16*0 33 0 0 33 4*0 6 0 0 6
  //   contents of rom_2 (hex, n*v repeats v):
  //   3f 0 0 0 22 22 0 0 20 0 2a 0 24 25 0 11 16*0 20 0 0 20 4*0 20 0 0 20
endmodule

module ALUControl (
  input  [4:0] SHAMT,
  input  [5:0] ALUop,
  input  [5:0] Func,
  output [10:0] ALUFunc
);

  wire and_1_out;

  Multiplexer #(.width(6)) multiplexer_1 (.in0(ALUop), .in1(Func), .out(ALUFunc[10:5]), .sel(and_1_out));
  and and_1 (and_1_out, ALUop[0], ALUop[1], ALUop[2], ALUop[4], ALUop[5], ALUop[3]);

  assign ALUFunc[4:0] = SHAMT;
endmodule

module sltkolo (
  input  [31:0] operand1,
  input  [31:0] operand2,
  output [31:0] out_3
);

  wire [30:0] subtractor_1_out;

  Subtractor #(.width(32)) subtractor_1 (
    .a(operand1), .b(operand2), .out({out_3[0], subtractor_1_out}));  // open: bin, bout

  assign out_3[31:1] = {31{1'b0}};
endmodule

module CLKmodul (
  input  CLK,
  input  RST,
  output phase0,
  output phase90
);

  wire d_ff_1_qn, d_ff_2_qn, not_1_out;

  D_Flip_Flop d_ff_1 (.D(d_ff_1_qn), .clk(CLK), .Q(phase0), .Qn(d_ff_1_qn), .reset(RST));  // open: preset
  D_Flip_Flop d_ff_2 (.D(d_ff_2_qn), .clk(not_1_out), .Q(phase90), .Qn(d_ff_2_qn), .reset(RST));  // open: preset
  not not_1 (not_1_out, CLK);
endmodule

module IF2ID (
  input  [31:0] PCin,
  input  [31:0] InsIn,
  output [31:0] NPC,
  output [31:0] Ins
);

  Register #(.width(32)) NextPC (.D(PCin), .Q(NPC));  // open: en, clk, clr
  Register #(.width(32)) Instruction (.D(InsIn), .Q(Ins));  // open: en, clk, clr
endmodule

module ID2EX (
  input  [31:0] InsIn,
  input  [31:0] OP1in,
  input  [31:0] OP2in,
  input  [31:0] SEin,
  input  [4:0] RegDstIn,
  input  [4:0] ALUOPIN,
  input  ALUSrcIN,
  input  RegDstMUXin,
  input  BranchIn,
  input  MemWriteIn,
  input  MemReadIn,
  input  RegWriteIn,
  input  MemToRegIn,
  output [31:0] Ins,
  output [31:0] OP1out,
  output [31:0] OP2out,
  output [31:0] SEout,
  output [4:0] RegDstOut,
  output [4:0] ALUOPOUT,
  output ALUSrcOut,
  output RegDstMUXout,
  output BranchOut,
  output MemWriteOut,
  output MemReadOut,
  output RegWriteOut,
  output MemToRegOut
);

  Register #(.width(32)) Instruction (.D(InsIn), .Q(Ins));  // open: en, clk, clr
  Register #(.width(32)) Operand1 (.D(OP1in), .Q(OP1out));  // open: en, clk, clr
  Register #(.width(32)) Operand2 (.D(OP2in), .Q(OP2out));  // open: en, clk, clr
  Register #(.width(32)) SignExtend (.D(SEin), .Q(SEout));  // open: en, clk, clr
  Register #(.width(5)) Destination (.D(RegDstIn), .Q(RegDstOut));  // open: en, clk, clr
  Register #(.width(5)) ALUOP (.D(ALUOPIN), .Q(ALUOPOUT));  // open: en, clk, clr
  D_Flip_Flop RegDstSignal (.D(RegDstMUXin), .Q(RegDstMUXout));  // open: clk, Qn, preset, reset
  D_Flip_Flop Branch (.D(BranchIn), .Q(BranchOut));  // open: clk, Qn, preset, reset
  D_Flip_Flop MemWrite (.D(MemWriteIn), .Q(MemWriteOut));  // open: clk, Qn, preset, reset
  D_Flip_Flop RegWrite (.D(RegWriteIn), .Q(RegWriteOut));  // open: clk, Qn, preset, reset
  D_Flip_Flop MemToReg (.D(MemToRegIn), .Q(MemToRegOut));  // open: clk, Qn, preset, reset
  D_Flip_Flop ALUSrc (.D(ALUSrcIN), .Q(ALUSrcOut));  // open: clk, Qn, preset, reset
  D_Flip_Flop MemRead (.D(MemReadIn), .Q(MemReadOut));  // open: clk, Qn, preset, reset

  // Notes on the sheet:
  //   EX GRUPA
  //   M Grupa
  //   W Grupa
endmodule

module EX2MEM (
  input  [31:0] AddrIn,
  input  [31:0] ResultIn,
  input  [31:0] RegIn,
  input  ZeroIn,
  input  [4:0] RegDstIn,
  input  BranchIn,
  input  MemWriteIn,
  input  MemReadIn,
  input  RegWriteIn,
  input  MemToRegIn,
  output [31:0] AddrOut,
  output [31:0] ResultOut,
  output [31:0] RegOut,
  output ZeroOut,
  output [4:0] RegDstOut,
  output BranchOut,
  output MemWriteOut,
  output MemReadOut,
  output RegWriteOut,
  output MemToRegOut
);

  Register #(.width(32)) BranchAddr (.D(AddrIn), .Q(AddrOut));  // open: en, clk, clr
  Register #(.width(32)) Result (.D(ResultIn), .Q(ResultOut));  // open: en, clk, clr
  Register #(.width(32)) RegisterFileRead (.D(RegIn), .Q(RegOut));  // open: en, clk, clr
  D_Flip_Flop ZeroFlag (.D(ZeroIn), .Q(ZeroOut));  // open: clk, Qn, preset, reset
  Register #(.width(5)) Destination (.D(RegDstIn), .Q(RegDstOut));  // open: en, clk, clr
  D_Flip_Flop Branch (.D(BranchIn), .Q(BranchOut));  // open: clk, Qn, preset, reset
  D_Flip_Flop MemWrite (.D(MemWriteIn), .Q(MemWriteOut));  // open: clk, Qn, preset, reset
  D_Flip_Flop MemRead (.D(MemReadIn), .Q(MemReadOut));  // open: clk, Qn, preset, reset
  D_Flip_Flop RegWrite (.D(RegWriteIn), .Q(RegWriteOut));  // open: clk, Qn, preset, reset
  D_Flip_Flop MemToReg (.D(MemToRegIn), .Q(MemToRegOut));  // open: clk, Qn, preset, reset

  // Notes on the sheet:
  //   M Grupa
  //   W Grupa
endmodule

module MEM2WB (
  input  [31:0] ResultIn,
  input  [31:0] DataIn,
  input  [4:0] RegDstIn,
  input  RegWriteIn,
  input  MemToRegIn,
  output [31:0] ResultOut,
  output [31:0] DataOut,
  output [4:0] RegDstOut,
  output RegWriteOut,
  output MemToRegOut
);

  Register #(.width(32)) Result (.D(ResultIn), .Q(ResultOut));  // open: en, clk, clr
  Register #(.width(32)) Data (.D(DataIn), .Q(DataOut));  // open: en, clk, clr
  Register #(.width(5)) Destination (.D(RegDstIn), .Q(RegDstOut));  // open: en, clk, clr
  D_Flip_Flop RegWrite (.D(RegWriteIn), .Q(RegWriteOut));  // open: clk, Qn, preset, reset
  D_Flip_Flop MemToReg (.D(MemToRegIn), .Q(MemToRegOut));  // open: clk, Qn, preset, reset

  // Notes on the sheet:
  //   W Grupa
endmodule
